# Fritzing sketch BigBreadBoard (saved by Fritzing 0.9.4)
breadboards: 3

parts:
  Breadboard4 = Breadboard Split Power
  Breadboard5 = Breadboard Split Power

nets:
  N1: Breadboard4.pin15Y, Breadboard4.pin17Y, Breadboard4.pin29Y, Breadboard5.pin3Y, Breadboard5.pin15Y, Breadboard5.pin17Y
  N2: Breadboard4.pin15Z, Breadboard4.pin17Z, Breadboard4.pin29Z, Breadboard5.pin3Z, Breadboard5.pin15Z, Breadboard5.pin17Z

custom parts:
  Breadboard Split Power: A custom 6 pin per group power supply strip where the top row (ground) is all bussed together and the bottom row (+V) is split in two groups of 12 pins. This version is modified to be a loadable part and was rescaled to be on the standard 1px = 1thou grid with the size set in inches
